# Fritzing sketch Arduino_Clock (saved by Fritzing 0.9.3b)
breadboards: 1

parts:
  S1 = Pushbutton [package="[THT]"]
  S2 = Pushbutton [package="[THT]"]
  S3 = Pushbutton [package="[THT]"]
  S4 = Pushbutton [package="[THT]"]
  S5 = Pushbutton [package="[THT]"]
  R1 = Resistor [tolerance=±5% resistance=220 package=THT]
  R2 = Resistor [tolerance=±5% resistance=220 package=THT]
  R3 = Resistor [tolerance=±5% resistance=220 package=THT]
  R4 = Resistor [tolerance=±5% resistance=220 package=THT]
  R5 = Resistor [tolerance=±5% resistance=220 package=THT]
  R6 = Resistor [tolerance=±5% resistance=220 package=THT]
  LCD1 = LCD screen
  Part1 = Arduino Uno (Rev3)
  LCM1602_IIC1 = LCM1602 IIC [part_number="LCM1602 IIC" chip_label="LCM1602 IIC" package="DIP (Dual Inline) [THT]"]
  U1 = SWITCH_SPDT [package=kps-1290]
  Part2 = Real Time Clock Module - DS1307 RTC Breakout Board

nets:
  N1: S1.Pin_1, S1.Pin_2, R5.Pin_0, Part1.D11_PWM/MOSI
  5V: S1.Pin_3, S1.Pin_4, S2.Pin_3, S2.Pin_4, S3.Pin_3, S3.Pin_4, S4.Pin_3, S4.Pin_4, S5.Pin_3, S5.Pin_4, Part1.5V, LCM1602_IIC1.VCC, U1.O, Part2.5V
  N2: S2.Pin_1, S2.Pin_2, R1.Pin_0, Part1.D9_PWM
  N3: S3.Pin_1, S3.Pin_2, R2.Pin_0, Part1.D8
  N4: S4.Pin_1, S4.Pin_2, R6.Pin_0, Part1.D12/MISO
  N5: S5.Pin_1, S5.Pin_2, R3.Pin_0, Part1.D10_PWM/SS
  GND: R1.Pin_1, R2.Pin_1, R3.Pin_1, R4.Pin_1, R5.Pin_1, R6.Pin_1, Part1.GND, LCM1602_IIC1.GND, U1.P, Part2.GND
  N6: R4.Pin_0, Part1.D13/SCK, U1.S
  VSS: LCD1.VSS, LCM1602_IIC1.VSS
  VDD: LCD1.VDD, LCM1602_IIC1.VDD
  N7: LCD1.V0, LCM1602_IIC1.V0
  N8: LCD1.RS, LCM1602_IIC1.RS
  N9: LCD1.R/W, LCM1602_IIC1.RW
  N10: LCD1.E, LCM1602_IIC1.E
  N11: LCD1.DB0, LCM1602_IIC1.D0
  N12: LCD1.DB1, LCM1602_IIC1.D1
  N13: LCD1.DB2, LCM1602_IIC1.D2
  N14: LCD1.DB3, LCM1602_IIC1.D3
  N15: LCD1.DB4, LCM1602_IIC1.D4
  N16: LCD1.DB5, LCM1602_IIC1.D5
  N17: LCD1.DB6, LCM1602_IIC1.D6
  N18: LCD1.DB7, LCM1602_IIC1.D7
  N19: LCD1.LED+, LCM1602_IIC1.A
  N20: LCD1.LED-, LCM1602_IIC1.K
  N21: Part1.A4/SDA, LCM1602_IIC1.SDA, Part2.SDA
  N22: Part1.A5/SCL, LCM1602_IIC1.SCL, Part2.SCL
  N23: LCM1602_IIC1.LED_A, LCM1602_IIC1.LED_B

custom parts:
  LCM1602 IIC: I2C-Module to use a 1602 or 2004 LCD on with the wire.h libory Serial LCD Modul
